# Fritzing sketch RPi2 IOT Core (saved by Fritzing 0.9.2b)
breadboards: 1

parts:
  S1 = Momentary Switch [package=ksa_sealed_tac_switch]
  Raspberry_Pi1 = Raspberry Pi 2

nets:
  N1: S1.2, Raspberry_Pi1.GPIO19, Raspberry_Pi1.GPIO26, Raspberry_Pi1.GND
  N2: S1.4, Raspberry_Pi1.ID_SD, Raspberry_Pi1.GPIO5, Raspberry_Pi1.GPIO6
